// Digital circuit CPU.dig as structural Verilog
module CPU (
);

  EEPROMDualPort #(.AddrBits(3), .Bits(8)) Operandos ();  // open: A, Din, str, C, ld, D
  EEPROMDualPort #(.AddrBits(3), .Bits(3)) \Operações  ();  // open: A, Din, str, C, ld, D
  ALU8bits alu8bits_1 ();  // open: N, S, CLK, MQ, neg, AC, Over

  // Notes on the sheet:
  //   contents of Operandos (hex, n*v repeats v):
  //   a,5,2,2
  //   contents of Operações (hex, n*v repeats v):
  //   0,1,2,3,4,5,6,7
endmodule
