// Digital circuit divisor8bits.dig as structural Verilog
module divisor8bits (
  input  [7:0] A,
  input  [7:0] B
);


  // Other names for the same wires on the sheet: D0 = A[0]; D1 = A[1]; D2 = A[2]; D3 = A[3]; D4 = A[4]; D5 = A[5];
  //   D6 = A[6]; D7 = A[7]; d0_t = B[0]; d1_t = B[1]; d2_t = B[2]; d3_t = B[3]; d4_t = B[4]; d5_t = B[5]; d6_t = B[6];
  //   d7_t = B[7]
endmodule
