// Digital circuit multiplicacao8bits.dig as structural Verilog
module multiplicacao8bits (
  input  [7:0] A,
  input  [7:0] B
);

  wire Cout0, Cout2, Cout3, Cout4, Cout5, Cout6, Cout7, Cout8, Cout9, Cout10, Cout11, Cout12, Cout13, Cout14,
       Cout15, Cout16, Cout17, Cout18, Cout19, Cout20, P0, P1, P2, P3, P4, P5, P6, PP0, PP1, PP2, PP3, PP4,
       PP5, PP6, PP7, PP8, PP9, PP10, PP11, PP12, PP13, PP14, PP15, PP16, PP17, PP18, PP19, PP20, PP21, PP22,
       PP23, PP24, PP25, PP26, SP0, SP1, SP2, SP3, SP4, SP5, SP6, SP7, SP8, SP9, SP10, SP11, SP12, SP13, SP14;

  // And and_1 has open pins: In_1=B[7], In_2=A[7], out=open
  // And and_2 has open pins: In_1=B[6], In_2=A[7], out=open
  // And and_3 has open pins: In_1=B[7], In_2=A[6], out=open
  // And and_4 has open pins: In_1=B[5], In_2=A[7], out=open
  // And and_5 has open pins: In_1=B[6], In_2=A[6], out=open
  // And and_6 has open pins: In_1=B[7], In_2=A[5], out=open
  // And and_7 has open pins: In_1=B[4], In_2=A[7], out=open
  // And and_8 has open pins: In_1=B[5], In_2=A[6], out=open
  // And and_9 has open pins: In_1=B[6], In_2=A[5], out=open
  // And and_10 has open pins: In_1=B[7], In_2=A[4], out=open
  // And and_11 has open pins: In_1=B[3], In_2=A[7], out=open
  // And and_12 has open pins: In_1=B[4], In_2=A[6], out=open
  // And and_13 has open pins: In_1=B[5], In_2=A[5], out=open
  // And and_14 has open pins: In_1=B[6], In_2=A[4], out=open
  // And and_15 has open pins: In_1=B[7], In_2=A[3], out=open
  // And and_16 has open pins: In_1=B[2], In_2=A[7], out=open
  // And and_17 has open pins: In_1=B[3], In_2=A[6], out=open
  // And and_18 has open pins: In_1=B[4], In_2=A[5], out=open
  // And and_19 has open pins: In_1=B[5], In_2=A[4], out=open
  // And and_20 has open pins: In_1=B[6], In_2=A[3], out=open
  // And and_21 has open pins: In_1=B[7], In_2=A[2], out=open
  // And and_22 has open pins: In_1=B[1], In_2=A[7], out=open
  // And and_23 has open pins: In_1=B[2], In_2=A[6], out=open
  // And and_24 has open pins: In_1=B[3], In_2=A[5], out=open
  // And and_25 has open pins: In_1=B[4], In_2=A[4], out=open
  // And and_26 has open pins: In_1=B[5], In_2=A[3], out=open
  // And and_27 has open pins: In_1=B[6], In_2=A[2], out=open
  // And and_28 has open pins: In_1=B[7], In_2=A[1], out=open
  // And and_29 has open pins: In_1=B[0], In_2=A[7], out=open
  // And and_30 has open pins: In_1=B[1], In_2=A[6], out=open
  // And and_31 has open pins: In_1=B[2], In_2=A[5], out=open
  // And and_32 has open pins: In_1=B[3], In_2=A[4], out=open
  // And and_33 has open pins: In_1=B[4], In_2=A[3], out=open
  // And and_34 has open pins: In_1=B[5], In_2=A[2], out=open
  // And and_35 has open pins: In_1=B[6], In_2=A[1], out=open
  // And and_36 has open pins: In_1=B[7], In_2=A[0], out=open
  and and_37 (PP20, B[0], A[6]);
  and and_38 (PP21, B[1], A[5]);
  and and_39 (PP22, B[2], A[4]);
  and and_40 (PP23, B[3], A[3]);
  and and_41 (PP24, B[4], A[2]);
  and and_42 (PP25, B[5], A[1]);
  and and_43 (PP26, B[6], A[0]);
  and and_44 (PP14, B[0], A[5]);
  and and_45 (PP15, B[1], A[4]);
  and and_46 (PP16, B[2], A[3]);
  and and_47 (PP17, B[3], A[2]);
  and and_48 (PP18, B[4], A[1]);
  and and_49 (PP19, B[5], A[0]);
  and and_50 (PP9, B[0], A[4]);
  and and_51 (PP10, B[1], A[3]);
  and and_52 (PP11, B[2], A[2]);
  and and_53 (PP12, B[3], A[1]);
  and and_54 (PP13, B[4], A[0]);
  and and_55 (PP5, B[0], A[3]);
  and and_56 (PP6, B[1], A[2]);
  and and_57 (PP7, B[2], A[1]);
  and and_58 (PP8, B[3], A[0]);
  and and_59 (PP2, B[0], A[2]);
  and and_60 (PP3, B[1], A[1]);
  and and_61 (PP4, B[2], A[0]);
  and and_62 (PP0, B[0], A[1]);
  and and_63 (PP1, B[1], A[0]);
  and and_64 (P0, B[0], A[0]);
  soma1bit PP0_plus_PP1 (.A(PP0), .B(PP1), .Cin(1'b0), .S(P1), .Cout(Cout0));
  soma1bit PP2_plus_PP3 (.A(PP2), .B(PP3), .Cin(Cout0), .S(SP0), .Cout(Cout11));
  soma1bit PP5_plus_PP6 (.A(PP5), .B(PP6), .Cin(Cout11), .S(SP1), .Cout(Cout3));
  soma1bit PP9_plus_PP10 (.A(PP9), .B(PP10), .Cin(Cout3), .S(SP3), .Cout(Cout6));
  soma1bit PP14_plus_PP15 (.A(PP14), .B(PP15), .Cin(Cout6), .S(SP6), .Cout(Cout10));
  soma1bit PP20_plus_PP21 (.A(PP20), .B(PP21), .Cin(Cout10), .S(SP10), .Cout(Cout15));
  soma1bit SP0_plus_PP4 (.A(SP0), .B(PP4), .Cin(1'b0), .S(P2), .Cout(Cout2));
  soma1bit SP1_plus_PP7 (.A(SP1), .B(PP7), .Cin(Cout2), .S(SP2), .Cout(Cout4));
  soma1bit SP3_plus_PP11 (.A(SP3), .B(PP11), .Cin(Cout4), .S(SP4), .Cout(Cout7));
  soma1bit SP6_plus_PP16 (.A(SP6), .B(PP16), .Cin(Cout7), .S(SP7), .Cout(Cout11));
  soma1bit SP10_plus_PP22 (.A(SP10), .B(PP22), .Cin(Cout11), .S(SP11), .Cout(Cout16));
  soma1bit SP2_plus_PP8 (.A(SP2), .B(PP8), .Cin(1'b0), .S(P3), .Cout(Cout5));
  soma1bit SP4_plus_PP12 (.A(SP4), .B(PP12), .Cin(Cout5), .S(SP5), .Cout(Cout8));
  soma1bit SP7_plus_PP17 (.A(SP7), .B(PP17), .Cin(Cout8), .S(SP8), .Cout(Cout12));
  soma1bit SP11_plus_PP23 (.A(SP11), .B(PP23), .Cin(Cout12), .S(SP12), .Cout(Cout17));
  soma1bit SP5_plus_PP13 (.A(SP5), .B(PP13), .Cin(1'b0), .S(P4), .Cout(Cout9));
  soma1bit SP8_plus_PP18 (.A(SP8), .B(PP18), .Cin(Cout9), .S(SP9), .Cout(Cout13));
  soma1bit SP12_plus_PP24 (.A(SP12), .B(PP24), .Cin(Cout13), .S(SP13), .Cout(Cout18));
  soma1bit SP9_plus_PP19 (.A(SP9), .B(PP19), .Cin(1'b0), .S(P5), .Cout(Cout14));
  soma1bit soma1bit_1 (.A(SP13), .B(PP25), .Cin(Cout14), .S(SP14), .Cout(Cout19));
  soma1bit soma1bit_2 (.A(SP14), .B(PP26), .Cin(1'b0), .S(P6), .Cout(Cout20));
endmodule
